// Logisim project ROM.circ as structural Verilog: 1 circuit, main circuit main
module main (
  output [7:0] DATA
);

  ROM rom_1 (.addr(8'h2), .data(DATA));  // open: sel

  // Notes on the sheet:
  //   contents of rom_1 (hex, n*v repeats v):
  //   11 22 33 44 55 66 77 88
endmodule
